# Fritzing sketch moon-phase-arduino-mega (saved by Fritzing 1.0.6)

parts:
  ZS-042_RTC1 = ZS-042 RTC Module
  Součástka1 = Arduino Mega 2560 (Rev3)
  LCD1 = TFT 2.2 inch 176x220 w SD
  C1 = Ceramic Capacitor [capacitance=100nF voltage=35V package="100 mil [THT, multilayer]"]
  LED1 = Super Flux RGB LED (com. anode)
  R3 = Resistor [tolerance=±5% resistance=220 package="0805 [SMD]"]
  R1 = Resistor [tolerance=±5% resistance=220 package="0805 [SMD]"]
  R2 = Resistor [tolerance=±5% resistance=220 package="0805 [SMD]"]
  C2 = Electrolytic Capacitor [capacitance=10μF voltage=35V package="0605 [SMD, electrolytic]"]

nets:
  GND: ZS-042_RTC1.GND, Součástka1.GND, C1.1, LED1.common_anode, C2.-
  VCC: ZS-042_RTC1.VCC, Součástka1.5V, LCD1.Pin_16, C1.0, C2.+
  N1: ZS-042_RTC1.SDA, Součástka1.D20/SDA, Součástka1.SDA
  N2: ZS-042_RTC1.SCL, Součástka1.D21/SCL
  N3: Součástka1.D10_PWM, LCD1.Pin_6
  N4: Součástka1.D9_PWM, LCD1.Pin_8
  N5: Součástka1.D8_PWM, LCD1.Pin_7
  N6: Součástka1.D5_PWM, R1.Pin_1
  N7: Součástka1.D6_PWM, R2.Pin_1
  N8: Součástka1.D7_PWM, R3.Pin_1
  N9: Součástka1.D51, LCD1.Pin_9
  N10: Součástka1.D52, LCD1.Pin_10
  N11: LED1.red_cathode, R1.Pin_0
  N12: LED1.blue_cathode, R3.Pin_0
  N13: LED1.green_cathode, R2.Pin_0

notes:
  VCC
  GND
  NC
  CLK
  SDA
  RS
  RST
  CS
  100nF
  10µF

custom parts:
  TFT 2.2 inch 176x220 w SD: This is a generic 1.8 tft spi lcd display available on ebay and others. .2.2-inch color screen,support 16BIT RGB 65K color display,display rich colors, 176x220 resolution.
